# Fritzing sketch WeatherUno (saved by Fritzing 0.9.3b)
breadboards: 1

parts:
  Part1 = Arduino Uno (Rev3)
  Nokia_5110_LCD_Module2 = Nokia5110LCDModule
  DHT1 = DHT22 Humidity and Temperature Sensor
  Part2 = BME280 Breakout  # not connected
  R1 = Resistor [tolerance=±5% resistance=220 package="0402 [SMD]"]
  R2 = Resistor [tolerance=±5% resistance=220 package="0402 [SMD]"]
  R3 = Resistor [tolerance=±5% resistance=220 package="0402 [SMD]"]

nets:
  N1: Part1.D8, Nokia_5110_LCD_Module2.D/C
  N2: Part1.D9_PWM, Nokia_5110_LCD_Module2.RST
  N3: Part1.D10_PWM/SS, Nokia_5110_LCD_Module2.SCE
  N4: Part1.D11_PWM/MOSI, Nokia_5110_LCD_Module2.Grnd
  N5: Part1.D12/MISO, Nokia_5110_LCD_Module2.Vcc
  N6: Part1.D2, DHT1.DATA, R1.Pin_0, R1.Pin_1
  N7: Part1.D7, Nokia_5110_LCD_Module2.SCLK, R3.Pin_0, R3.Pin_1
  N8: Part1.3V3, Nokia_5110_LCD_Module2.6_DN_(MOSI)
  5V: Part1.5V, DHT1.VDD
  GND: Part1.GND, Nokia_5110_LCD_Module2.LED, DHT1.GND, R2.Pin_1

notes:
  Create 2 power rails. One for 5v and the second for 3.3v
  BME- Pulling SD0 to Gnd for address 0x76. Use 4k7 resistor to ground. Your sensor layout may vary, but the pins will be labeled the same.
  5v Rail
  3.3v Rail
  LCD is using 330 Ohm resistor between the Bkl pin and pin 7 on the Arduino
  DHT - place 10k resistor between data pin and Arduino pin.

custom parts:
  : Nokia 5110 LCD with 8 pin. It's a 45mm*45mm module part. Description: The Nokia 5110 is a basic graphic LCD screen for lots of applications. It was originally intended for as a cell phone screen. This one is mounted on an easy to solder PCB. It uses the PCD8544 controller. The PCD8544 is a low power CMOS LCD controller/driver, designed to drive a graphic display of 48 rows and 84 columns. All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
